# Fritzing sketch HandRemote-WiringDiagram (saved by Fritzing 0.9.3b)

parts:
  Part1 = Arduino Uno (Rev3)
  Part3 = Arduino Xbee Libellium Shield
  DFRobot_LCD_keypad_shield1 = LCD keypad Shield
  BuzzerDFR1 = BuzzerDFR0032
  R1 = Resistor [tolerance=±5% resistance=220k package=THT]
  R2 = Resistor [tolerance=±5% resistance=220 package=THT]
  S1 = Toggle Switch [package=THT]  # not connected
  VCC1 = Battery block 9V  # not connected

nets:
  N1: Part1.A1, DFRobot_LCD_keypad_shield1.A1, R1.Pin_1, R2.Pin_1
  N2: Part1.D8, DFRobot_LCD_keypad_shield1.D13
  N3: Part1.D4, DFRobot_LCD_keypad_shield1.D2
  N4: Part1.D5_PWM, DFRobot_LCD_keypad_shield1.D3
  N5: Part1.D6_PWM, DFRobot_LCD_keypad_shield1.D11
  N6: Part1.D7, DFRobot_LCD_keypad_shield1.D12
  N7: Part3.M8RXD, Part3.2, DFRobot_LCD_keypad_shield1.D0
  N8: Part3.M8TXD, Part3.DOUT, DFRobot_LCD_keypad_shield1.D1
  N9: DFRobot_LCD_keypad_shield1.GND#4, R2.Pin_0
  N10: DFRobot_LCD_keypad_shield1.Vin, R1.Pin_0
  N11: DFRobot_LCD_keypad_shield1.GND#22, BuzzerDFR1.GND
  VCC: DFRobot_LCD_keypad_shield1.VCC, BuzzerDFR1.5V

notes:
  Active Buzzer
  D12 = Signal
  D13 = 5Vdc+
  GND = GND
  Voltage Divider for Battery Meter (A1)
  VIN > R1 > A1
  A1> R2 > GND
  XBee DIN>TX(D2)
  XBee DOUT>RX(D3)
  Used Pins **
  D10 - LCD Backlight
  D9 - LCD Enable
  D8 - LCD RS
  D7 to D4 - LCD DB(0::4)
  Used Pin
  A0 - Keypad Buttons
  A1 - Batt Monitor

custom parts:
  LCD keypad Shield: A 2 row LCD shield with buttons, and contrast regulator.
