# Fritzing sketch PumpController-ArduinoStack (saved by Fritzing 0.9.3b)
perfboards: 1

parts:
  Part1 = Arduino Uno (Rev3)
  Part2 = Arduino Xbee Libellium Shield
  Part3 = JeePlug experimenter's board
  Part4 = JeePlug experimenter's board
  Part5 = JeePlug experimenter's board
  Part6 = JeePlug experimenter's board
  Part7 = JeePlug experimenter's board
  Part8 = JeePlug experimenter's board
  BAT1 = BC9VPC [package=bc9vpc]
  Part9 = NCP1400 Step-Up Breakout
  LTR_1 = Monacor line transformer [part_number=LTR-110]
  U1 = SWITCH_SPDT [package=kps-1290]
  J14 = Camdenboss CTB0158-3 [part_number=CTB0158-3 package=THT]
  J17 = Camdenboss CTB0158-3 [part_number=CTB0158-3 package=THT]
  J18 = Camdenboss CTB0158-3 [part_number=CTB0158-3 package=THT]
  J19 = Camdenboss CTB0158-3 [part_number=CTB0158-3 package=THT]
  J20 = Camdenboss CTB0158-4 [part_number=CTB0158-4 package=THT]
  J21 = Camdenboss CTB0158-4 [part_number=CTB0158-4 package=THT]
  J22 = Camdenboss CTB0158-4 [part_number=CTB0158-4 package=THT]
  J23 = Camdenboss CTB0158-4 [part_number=CTB0158-4 package=THT]
  Power_plug1 = Power plug
  D1 = Rectifier Diode [part_number=1N4001 package="300 mil [THT]"]
  D2 = Rectifier Diode [part_number=1N4001 package="300 mil [THT]"]  # not connected
  R1 = Resistor [tolerance=±5% resistance=220 package=THT]
  R2 = Resistor [tolerance=±5% resistance=220 package=THT]
  J24 = Camdenboss CTB0158-4 [part_number=CTB0158-4 package=THT]

nets:
  N1: Part1.A0, Part2.A0, Part3.N$64, Part5.N$24, J19.pin3
  N2: Part1.A1, Part2.A1, Part3.N$30, Part5.A1, J19.pin2
  N3: Part1.A2, Part2.A2, Part3.N$28, Part5.A2, J19.pin1
  N4: Part1.A3, Part2.A3, Part3.N$25, Part5.A3, J18.pin3
  N5: Part1.A4/SDA, Part2.A4, Part4.N$64, Part5.A4, Part8.B1, J18.pin2
  N6: Part1.A5/SCL, Part2.A5, Part4.N$30, Part5.A5, Part8.B2, J18.pin1
  N7: Part1.D8, Part7.B1, Part7.N$14, J17.pin1
  N8: Part1.D9_PWM, Part7.B2, Part7.N$57, J17.pin2
  N9: Part1.D10_PWM/SS, Part7.B3, Part8.N$10, J17.pin3
  N10: Part1.D11_PWM/MOSI, Part7.B4, Part8.N$12, J14.pin1
  N11: Part1.D12/MISO, Part7.B5, Part8.N$14, J14.pin2
  N12: Part1.D13/SCK, Part7.B6, Part8.N$57, J14.pin3
  N13: Part1.GND, Part7.N$8
  N14: Part1.AREF, Part8.N$9
  N15: Part1.D2, Part2.D2, Part2.2, Part6.B2, Part6.N$55
  N16: Part1.D3_PWM, Part2.D3, Part2.DOUT, Part6.B3, Part6.N$23
  N17: Part1.D4, Part2.D4, Part6.B4, Part6.N$11, J20.pin1
  N18: Part1.D5_PWM, Part2.D5, Part6.B5, Part6.N$13, J20.pin2
  N19: Part1.D6_PWM, Part2.D6, Part6.B6, Part6.N$15, J20.pin3
  N20: Part1.D7, Part2.D7, Part6.N$8, Part7.N$55, J20.pin4
  N21: Part2.+5V, Part4.N$31, Part6.A1, J22.pin4
  N22: Part2.GND, Part5.N$16, Part5.N$33, Part6.N$41, J21.pin1, J21.pin4
  N23: Part4.N$7, J22.pin3
  N24: Part5.N$17, J21.pin2
  N25: Part6.A2, J21.pin3
  N26: Part7.N$24, J22.pin2
  N27: Part7.N$39, J22.pin1
  N28: BAT1.V+, U1.P
  GND: BAT1.V-, Part9.GND, LTR_1.GND, J23.pin1, J23.pin3, Power_plug1.GND, R2.Pin_1
  N29: Part9.VOUT, J23.pin4
  N30: Part9.VIN, LTR_1.02
  N31: U1.S, J23.pin2, D1.anode
  N32: D1.cathode, R1.Pin_0, J24.pin3
  N33: R1.Pin_1, R2.Pin_0, J24.pin2

notes:
  Vdc Plug
  Fulree 3005ADJ DC/DC Convertor
  RHINO 480VAC 3-phase Power Supply
  9V Backup Battery
  Dual Power with Monitor Divider
  Monitor Pin
  10Vdc
  24Vdc
  GND BANK
  5Vdc BANK
  RX/TX SoftSerial
  D4-D7
  D8-D13
  A5
  UN-USED RX/TX
